# Fritzing sketch tic_tac_toe_circuit (saved by Fritzing 0.9.5d)
breadboards: 1

parts:
  S1_LEFT = Pushbutton [package="[THT]"]
  S2_RIGHT = Pushbutton [package="[THT]"]
  S3_ENTER = Pushbutton [package="[THT]"]
  R1 = Resistor [tolerance=±5% resistance=220 package=THT]
  R2 = Resistor [tolerance=±5% resistance=220 package=THT]
  S5_UP = Pushbutton [package=THT]
  S6_DOWN = Pushbutton [package=THT]
  R4 = Resistor [tolerance=±5% resistance=220 package=THT]
  R3 = Resistor [tolerance=±5% resistance=220 package=THT]
  Part1 = Arduino Uno (Rev3)
  LED1 = LED - 5mm [color="Red (633nm)" package="5 mm [THT]"]
  LED2 = LED - 5mm [color="Green (570nm)" package="5 mm [THT]"]
  LED3 = LED - 5mm [color="Yellow (595nm)" package="5 mm [THT]"]
  R6 = Resistor [tolerance=±5% resistance=220 package=THT]
  R7 = Resistor [tolerance=±5% resistance=220 package=THT]
  R8 = Resistor [tolerance=±5% resistance=220 package=THT]
  Part2 = LED Matrix - Serial Interface - Red/Green/Blue
  J1 = Piezo Speaker
  R5 = Resistor [tolerance=±5% resistance=220 package=THT]

nets:
  N1: S1_LEFT.Pin_1, S1_LEFT.Pin_2, R1.Pin_0, Part1.D2
  5V: S1_LEFT.Pin_3, S1_LEFT.Pin_4, S2_RIGHT.Pin_3, S2_RIGHT.Pin_4, S3_ENTER.Pin_3, S3_ENTER.Pin_4, S5_UP.leg1, S6_DOWN.leg1, Part1.5V, Part2.VCC
  N2: S2_RIGHT.Pin_1, S2_RIGHT.Pin_2, R3.Pin_1, Part1.D4
  N3: S3_ENTER.Pin_1, S3_ENTER.Pin_2, Part1.D6_PWM, R5.Pin_1
  GND: R1.Pin_1, R2.Pin_1, R4.Pin_0, R3.Pin_0, Part1.GND, LED1.anode, LED2.anode, LED3.anode, Part2.GND, J1.pin2, R5.Pin_0
  N4: R2.Pin_0, S5_UP.leg0, Part1.D3_PWM
  N5: S6_DOWN.leg0, R4.Pin_1, Part1.D5_PWM
  N6: Part1.D8, R7.Pin_0
  N7: Part1.D9_PWM, R6.Pin_0
  N8: Part1.D10_PWM/SS, Part2.CS
  N9: Part1.D11_PWM/MOSI, Part2.MOSI
  N10: Part1.D12/MISO, J1.pin1
  N11: Part1.D13/SCK, Part2.SCK
  N12: Part1.D7, R8.Pin_0
  N13: LED1.cathode, R8.Pin_1
  N14: LED2.cathode, R7.Pin_1
  N15: LED3.cathode, R6.Pin_1
